# Fritzing sketch circuit (saved by Fritzing 0.9.3b)
breadboards: 1

parts:
  Componente1 = Arduino Uno (Rev3) - ICSP
  R1 = Resistor [tolerance=±2% resistance=1k package="0402 [SMD]"]
  R2 = Resistor [tolerance=±2% resistance=1k package="0402 [SMD]"]
  S1 = Pushbutton [package="[SMD]"]
  S2 = Pushbutton [package="[SMD]"]
  S3 = Pushbutton [package="[SMD]"]
  R3 = Resistor [tolerance=±2% resistance=1k package="0402 [SMD]"]
  J1 = Piezo Speaker

nets:
  N1: Componente1.A0, R1.Pin_0, S3.Pin_1, S3.Pin_2
  N2: Componente1.A1, R2.Pin_0, S2.Pin_1, S2.Pin_2
  N3: Componente1.A2, S1.Pin_1, S1.Pin_2, R3.Pin_0
  N4: Componente1.5V, S1.Pin_3, S1.Pin_4, S2.Pin_3, S2.Pin_4, S3.Pin_3, S3.Pin_4
  N5: Componente1.D5_PWM, J1.pin2
  N6: Componente1.GND, R1.Pin_1, R2.Pin_1, R3.Pin_1, J1.pin1
